# Fritzing sketch pnp_test (saved by Fritzing 1.0.5)
circuit board: 8.46667cm x 5.64444cm
breadboards: 1

parts:
  R3 = Resistor [tolerance=±5% power=0.25W resistance=220 package=THT]  # not connected
  R1 = Resistor [tolerance=±5% resistance=220 power=0.25W package="2512 [SMD]"]  # not connected
  R4 = Resistor [tolerance=±5% power=0.25W resistance=220 package=THT]
  R5 = Resistor [tolerance=±5% resistance=220 power=0.25W package="2512 [SMD]"]  # not connected
  R6 = Resistor [tolerance=±5% power=0.25W resistance=220 package=THT]  # not connected
  R7 = Resistor [tolerance=±5% resistance=220 power=0.25W package="2512 [SMD]"]  # not connected
  U1 = 555 Timer [package="DIP8 [THT]"]
  U2 = 555 Timer [package="SO8 [SMD]"]  # not connected
  U3 = 555 Timer [package="DIP8 [THT]"]
  U4 = 555 Timer [package="SO8 [SMD]"]  # not connected
  U5 = 555 Timer [package="DIP8 [THT]"]
  U6 = 555 Timer [package="SO8 [SMD]"]
  C1 = Ceramic Capacitor [capacitance=100nF voltage=35V package="100 mil [THT, multilayer]"]  # not connected
  C2 = Ceramic Capacitor [capacitance=100nF voltage=35V package="200 mil [THT, multilayer]"]
  C3 = Ceramic Capacitor [capacitance=100nF voltage=35V package="0603 [SMD, multilayer]"]  # not connected
  C4 = Ceramic Capacitor [capacitance=100nF voltage=35V package="1206 [SMD, multilayer]"]
  Pad1 = Pad [width=7.902222222222222 height=9.03111111111111 connect=center]  # not connected

nets:
  N1: R4.Pin_0, C2.0
  N2: U1.Output, U5.Discharge
  N3: U1.Reset, U5.Vcc_Supply_Voltage
  N4: U3.Ground, C4.0
  N5: U3.Trigger, C4.1
  N6: U5.Reset, U6.Pin_8
